# Fritzing sketch Diagrama de conexión (saved by Fritzing 0.9.3b)
breadboards: 1

parts:
  U1 = ESP8266 WiFi Module [part_number=ESP8266]
  Control_de_humedad = Humidity and Temperature Sensor RHT03
  Motor_de_bomba_hidraulica = Stepper Motor - Bipolar  # not connected
  Raspberry_Pi_1 = Raspberry Pi 3 [part_number=RPI-3-V1.2]  # not connected

nets:
  N1: U1.D3, Control_de_humedad.Data-signal
  N2: U1.3.3V#10, Control_de_humedad.Vcc
  N3: U1.GND#12, Control_de_humedad.GND_1
